# Fritzing sketch Plain (saved by Fritzing 0.9.3b)
circuit board: 2.5cm x 2.5cm
breadboards: 1

parts:
  TINY85 = IC, DIP package, 8 pins [chip_label=IC]
  ON/OFF = female pin header, 3 pins [form="♀ (female)"]
  BAT1 = Battery Holders [package=battcom_20mm_pth]

nets:
  N1: TINY85.pin4, BAT1.-
  N2: TINY85.pin8, ON/OFF.pin2, ON/OFF.pin3
  N3: ON/OFF.pin1, BAT1.+

notes:
  HackBerry
  Plain 1.0
